// Logisim project 4 Bit Adder.circ as structural Verilog: 2 circuits, main circuit Full Adder
module Full_Adder (
  input  A,
  input  B,
  input  C_IN,
  output SUM,
  output C_Out
);

  wire and_1_out, and_2_out, xor_1_out;

  xor xor_1 (xor_1_out, A, B);
  and and_1 (and_1_out, A, B);
  and and_2 (and_2_out, xor_1_out, C_IN);
  xor xor_2 (SUM, xor_1_out, C_IN);
  or or_1 (C_Out, and_1_out, and_2_out);

  // Notes on the sheet:
  //   FULL ADDER
endmodule

module _4_bit_adder (
  input  B0,
  input  A0,
  input  B1,
  input  A1,
  input  B2,
  input  A2,
  input  B3,
  input  A3,
  input  CARRY_BIT,
  output C_OUT,
  output S0,
  output S1,
  output S2,
  output S3
);

  wire full_adder_1_c_out, full_adder_2_c_out, full_adder_3_c_out;

  Full_Adder full_adder_1 (.A(A0), .B(B0), .C_IN(CARRY_BIT), .SUM(S0), .C_Out(full_adder_1_c_out));
  Full_Adder full_adder_2 (.A(A1), .B(B1), .C_IN(full_adder_1_c_out), .SUM(S1), .C_Out(full_adder_2_c_out));
  Full_Adder full_adder_3 (.A(A2), .B(B2), .C_IN(full_adder_2_c_out), .SUM(S2), .C_Out(full_adder_3_c_out));
  Full_Adder full_adder_4 (.A(A3), .B(B3), .C_IN(full_adder_3_c_out), .SUM(S3), .C_Out(C_OUT));

  // Notes on the sheet:
  //   4 BIT ADDER
endmodule
