// Logisim project 4-BITS( CPU).circ as structural Verilog: 3 circuits, main circuit main
module main (
  input  in_1
);

  wire CLK, DATA, MOV;
  wire [1:0] OP;
  wire [2:0] RA, RB, RD;
  wire [3:0] alu_1_output, controlled_buffer_1_out, counter_1_q, counter_1_q_2, register_file_1_p6,
       register_file_1_p7;
  wire [15:0] rom_1_data;
  wire [15:9] register_1_q;

  Clock clock_1 (.out(CLK));
  Hex_Digit_Display hex_digit_display_1 (.value(counter_1_q_2));  // open: dp
  Counter counter_1 (
    .load(1'b0), .count(1'b1), .Q({counter_1_q_2, counter_1_q}), .clk(CLK), .clr(in_1));  // open: D, carry
  assign controlled_buffer_1_out = MOV ? {RA[0], RB} : 4'bz;  // Controlled_Buffer controlled_buffer_1
  Hex_Digit_Display hex_digit_display_2 (.value(counter_1_q));  // open: dp
  ROM #(.dataWidth(16)) rom_1 (.addr({counter_1_q_2, counter_1_q}), .data(rom_1_data));  // open: sel
  assign controlled_buffer_1_out = DATA ? alu_1_output : 4'bz;  // Controlled_Buffer controlled_buffer_2
  // Register_File register_file_1: pin names not known; wires that end beside it: controlled_buffer_1_out, RD, RA, RB, CLK, register_file_1_p6, register_file_1_p7
  ALU alu_1 (.A(register_file_1_p6), .B(register_file_1_p7), .OP(OP), .Output(alu_1_output));
  Register #(.width(16)) register_1 (
    .D(rom_1_data), .en(1'b1), .Q({register_1_q[15:14], OP, register_1_q[11:9], RA, RB, RD}), .clk(CLK));  // open: clr
  and and_1 (DATA, ~register_1_q[14], ~register_1_q[15]);  // AND_Gate
  and and_2 (MOV, register_1_q[14], register_1_q[15]);

  // Other names for the same wires on the sheet: Value[3:0] = {RA[0], RB}

  // Notes on the sheet:
  //   contents of rom_1 (hex, n*v repeats v):
  //   c024 c02a 117 3116
endmodule

module ALU (
  input  [3:0] A,
  input  [3:0] B,
  input  [1:0] OP,
  output [3:0] Output
);

  wire [3:0] adder_1_out, and_1_out, or_1_out, xor_1_out;

  Adder #(.width(4)) adder_1 (.a(A), .b(B), .out(adder_1_out), .cin(1'b0));  // open: cout
  assign or_1_out = A | B;  // OR_Gate or_1, 4 bits wide
  assign and_1_out = A & B;  // AND_Gate and_1, 4 bits wide
  assign xor_1_out = A ^ B;  // XOR_Gate xor_1, 4 bits wide
  Multiplexer #(.select(2), .width(4), .disabled(0), .enable("false")) multiplexer_1 (
    .in0(adder_1_out), .in1(or_1_out), .in2(and_1_out), .in3(xor_1_out), .out(Output), .sel(OP));
endmodule

// RegFile
module Register_File (
  input  [3:0] INP,
  input  C,
  input  [2:0] RA,
  input  [2:0] RD,
  input  [2:0] RB,
  output [3:0] BUS_A,
  output [3:0] BUS_B
);

  wire demultiplexer_1_out0, demultiplexer_1_out1, demultiplexer_1_out2, demultiplexer_1_out3,
       demultiplexer_1_out4, demultiplexer_1_out5, demultiplexer_1_out6, demultiplexer_1_out7;
  wire [3:0] R0_q, R1_q, R2_q, R3_q, R4_q, R5_q, R6_q, R7_q;

  Demultiplexer #(.select(3)) demultiplexer_1 (
    .out0(demultiplexer_1_out0), .out1(demultiplexer_1_out1), .out2(demultiplexer_1_out2),
    .out3(demultiplexer_1_out3), .out4(demultiplexer_1_out4), .out5(demultiplexer_1_out5),
    .out6(demultiplexer_1_out6), .out7(demultiplexer_1_out7), .in(1'b1), .sel(RD));  // open: en
  Register #(.width(4)) R0 (.D(INP), .en(demultiplexer_1_out0), .Q(R0_q), .clk(C));  // open: clr
  Register #(.width(4)) R1 (.D(INP), .en(demultiplexer_1_out1), .Q(R1_q), .clk(C));  // open: clr
  Register #(.width(4)) R2 (.D(INP), .en(demultiplexer_1_out2), .Q(R2_q), .clk(C));  // open: clr
  Register #(.width(4)) R3 (.D(INP), .en(demultiplexer_1_out3), .Q(R3_q), .clk(C));  // open: clr
  Register #(.width(4)) R4 (.D(INP), .en(demultiplexer_1_out4), .Q(R4_q), .clk(C));  // open: clr
  Register #(.width(4)) R5 (.D(INP), .en(demultiplexer_1_out5), .Q(R5_q), .clk(C));  // open: clr
  Register #(.width(4)) R6 (.D(INP), .en(demultiplexer_1_out6), .Q(R6_q), .clk(C));  // open: clr
  Register #(.width(4)) R7 (.D(INP), .en(demultiplexer_1_out7), .Q(R7_q), .clk(C));  // open: clr
  Multiplexer #(.select(3), .width(4)) multiplexer_1 (
    .in0(R0_q), .in1(R1_q), .in2(R2_q), .in3(R3_q), .in4(R4_q), .in5(R5_q), .in6(R6_q), .in7(R7_q),
    .out(BUS_B), .sel(RB));  // open: en
  Multiplexer #(.select(3), .width(4)) multiplexer_2 (
    .in0(R0_q), .in1(R1_q), .in2(R2_q), .in3(R3_q), .in4(R4_q), .in5(R5_q), .in6(R6_q), .in7(R7_q),
    .out(BUS_A), .sel(RA));  // open: en
endmodule
