// Logisim project Demultiplexer.circ as structural Verilog: 1 circuit, main circuit main
module main (
  input  A,
  input  B,
  input  Fixed_input_D
);

  wire and_1_out, and_2_out, and_3_out, and_4_out, not_1_out, not_2_out;

  not not_1 (not_1_out, A);
  not not_2 (not_2_out, B);
  and and_1 (and_1_out, Fixed_input_D, not_2_out, not_1_out);
  LED led_1 (.in(and_1_out));
  LED led_2 (.in(and_2_out));
  and and_2 (and_2_out, Fixed_input_D, not_2_out, A);
  LED led_3 (.in(and_3_out));
  and and_3 (and_3_out, Fixed_input_D, B, not_1_out);
  and and_4 (and_4_out, Fixed_input_D, B, A);
  LED led_4 (.in(and_4_out));

  // Notes on the sheet:
  //   Demultiplexer
endmodule
