// Logisim project HALF & FULL Adder.circ as structural Verilog: 1 circuit, main circuit main
module main (
  input  A,
  input  B,
  input  A_2,
  input  B_2,
  input  C_in,
  output SUM,
  output CARRY,
  output SUM_2,
  output C_out
);

  wire and_1_out, and_3_out, xor_1_out;

  xor xor_1 (xor_1_out, A_2, B_2);
  and and_1 (and_1_out, A_2, B_2);
  xor xor_2 (SUM, A, B);
  and and_2 (CARRY, A, B);
  and and_3 (and_3_out, xor_1_out, C_in);
  xor xor_3 (SUM_2, xor_1_out, C_in);
  or or_1 (C_out, and_1_out, and_3_out);

  // Notes on the sheet:
  //   HALF ADDER
  //   FULL ADDER
endmodule
