// Logisim project HALF & FULL SUBTRACTOR.circ as structural Verilog: 1 circuit, main circuit main
module main (
  input  A,
  input  B,
  input  A_2,
  input  B_2,
  input  Borrow_In,
  output DIFFER,
  output BORROW,
  output DIFFER_2,
  output Borrow__Out
);

  wire and_1_out, and_2_out, not_1_out, not_2_out, not_3_out, undriven, xor_1_out;

  not not_1 (not_1_out, A_2);
  xor xor_1 (xor_1_out, A_2, B_2);
  not not_2 (not_2_out, xor_1_out);
  xor xor_2 (DIFFER, A, B);
  not not_3 (not_3_out, A);
  and and_1 (and_1_out, not_2_out, Borrow_In);
  and and_2 (and_2_out, not_1_out, B_2);
  and and_3 (BORROW, not_3_out, B);
  xor xor_3 (DIFFER_2, xor_1_out, Borrow_In);
  or or_1 (Borrow__Out, and_1_out, undriven, and_2_out);

  // Notes on the sheet:
  //   HALF SUBTRATOR
  //   FULL SUBTRACTOR
endmodule
