// Logisim project JK Flip-Flop.circ as structural Verilog: 1 circuit, main circuit main
module main (
  input  in_1,
  input  in_2,
  output OUTPUT_1,
  output OUTPUT_2
);

  wire and_1_out, and_2_out, and_3_out, clock_1_out, nand_1_out, nor_1_out, nor_2_out, not_1_out;

  Clock clock_1 (.out(clock_1_out));
  not not_1 (not_1_out, clock_1_out);
  nand nand_1 (nand_1_out, OUTPUT_1, in_1, clock_1_out);
  and and_1 (and_1_out, clock_1_out, in_2, OUTPUT_2);
  nor nor_1 (nor_1_out, nand_1_out, nor_2_out);
  nor nor_2 (nor_2_out, nor_1_out, and_1_out);
  and and_2 (and_2_out, nor_1_out, nor_1_out, not_1_out);
  and and_3 (and_3_out, not_1_out, nor_2_out);
  nor nor_3 (OUTPUT_1, and_2_out, OUTPUT_2);
  nor nor_4 (OUTPUT_2, OUTPUT_1, and_3_out);

  // Notes on the sheet:
  //   JK Flip-Flop
endmodule
