// Logisim project Multiplexer.circ as structural Verilog: 1 circuit, main circuit main
module main (
  input  Input_1,
  input  sum,
  input  Input_2
);

  wire and_1_out, and_2_out, not_1_out, or_1_out;

  not not_1 (not_1_out, sum);
  and and_1 (and_1_out, Input_1, sum);
  and and_2 (and_2_out, Input_2, not_1_out);
  or or_1 (or_1_out, and_1_out, and_2_out);
  LED led_1 (.in(or_1_out));

  // Notes on the sheet:
  //   Multiplexer
endmodule
