// Logisim project NAND NOR XOR.circ as structural Verilog: 1 circuit, main circuit main
module main (
  input  in_1,
  input  in_2,
  input  in_3,
  input  in_4,
  input  in_5,
  input  in_6
);

  wire and_1_out, and_2_out, and_3_out, not_1_out, not_2_out, not_3_out, not_4_out, or_1_out, or_2_out;

  not not_1 (not_1_out, in_5);
  not not_2 (not_2_out, in_6);
  and and_1 (and_1_out, in_1, in_2);
  or or_1 (or_1_out, in_3, in_4);
  and and_2 (and_2_out, in_5, not_2_out);
  and and_3 (and_3_out, not_1_out, in_6);
  not not_3 (not_3_out, and_1_out);
  not not_4 (not_4_out, or_1_out);
  LED led_1 (.in(not_4_out));
  or or_2 (or_2_out, and_2_out, and_3_out);
  LED led_2 (.in(not_3_out));
  LED led_3 (.in(or_2_out));

  // Notes on the sheet:
  //   NOR
  //   XOR
  //   NAND
endmodule
