// Logisim project SR Flip-Flop.circ as structural Verilog: 1 circuit, main circuit main
module main (
  input  in_1,
  input  in_2,
  input  in_3,
  output OUTPUT_1,
  output OUTPUT_2
);

  wire and_1_out, and_2_out;

  and and_1 (and_1_out, in_1, in_1, in_2);
  and and_2 (and_2_out, in_2, in_3);
  nor nor_1 (OUTPUT_1, and_1_out, OUTPUT_2);
  nor nor_2 (OUTPUT_2, OUTPUT_1, and_2_out);

  // Notes on the sheet:
  //   SR Flip-Flop
endmodule
